// Logisim project MyCPU1.circ as structural Verilog: 5 circuits, main circuit main
module main (
  input  \Сброс ,
  input  \Останов ,
  input  \Вход_счетчика_команд ,
  input  \Включение_счетча_команд ,
  input  \Вход_адресного_ресистра ,
  input  \Выход_счетика_команд ,
  input  \Очистка_памяти ,
  input  \Чтение_из_памяти ,
  input  \Запись_в_память ,
  input  \Вход_командного_регистра ,
  input  \Выход_ком_регистра ,
  input  \Выход_сумматора ,
  input  \сброс_флагов ,
  input  \флаг_больше ,
  input  \флаг_меньше ,
  input  \Вход_JR ,
  input  \Выход_JR ,
  input  \вход_RTSK ,
  output [7:0] \Шина 
);

  wire and_10_out, and_11_out, and_12_out, and_13_out, controlled_buffer_2_out, not_1_out, or_1_out,
       or_2_out, or_3_out, or_4_out, \с8_1_a_b_2 , \с8_1_a_b_3 , \с81_1_a_b_2 , \с81_1_a_b_3 ,
       \Тактовый_генератор_out ;
  wire [2:0] \Счетчик_команд_q ;
  wire [3:0] bit_extender_1_out, bit_extender_2_out, bit_extender_3_out, bit_extender_4_out,
       bit_extender_5_out;
  wire [7:0] adder_1_out, adder_2_out, adder_3_out, and_7_out, and_9_out, decoder_1_out0, JR_q, ram_1_data,
       RTSK_q, xor_1_out, \Адресный_регистр_q , \Командный_регистр_q , \Регистр_0_q , \Регистр_1_q ,
       \Регистр_3_q , \Регистр_4_q , \Регистр_5_q , \Счетчик_команд_2_q ;
  wire [7:1] pull_resistor_6_node;
  wire [7:7] rom_1_data_2;
  wire [15:0] divider_1_out, divider_1_rem, divider_2_out, divider_2_rem, divider_3_out, divider_3_rem,
       divider_4_out, divider_4_rem, register_1_q;
  wire [15:8] \Регистр_2_q ;
  wire [17:0] rom_1_data;

  not not_1 (not_1_out, \Останов );
  Counter #(.width(3), .max('h5), .trigger("falling")) \u_Счетчик_команд  (
    .Q(\Счетчик_команд_q ), .clk(controlled_buffer_2_out), .clr(\Сброс ));  // open: load, D, count, carry
  Counter \u_Счетчик_команд_2  (
    .load(rom_1_data[0]), .D(\Шина ), .count(rom_1_data[14]), .Q(\Счетчик_команд_2_q ),
    .clk(controlled_buffer_2_out), .clr(\Сброс ));  // open: carry
  Register \u_Командный_регистр  (
    .D(\Шина ), .en(rom_1_data[13]), .Q(\Командный_регистр_q ), .clk(controlled_buffer_2_out), .clr(\Сброс ));
  and and_1 (and_9_out[6], decoder_1_out0[6], rom_1_data[7]);
  and and_2 (and_9_out[7], decoder_1_out0[7], rom_1_data[7]);
  Decoder #(.select(3)) decoder_1 (
    .out0(decoder_1_out0[0]), .out1(decoder_1_out0[1]), .out2(decoder_1_out0[2]), .out3(decoder_1_out0[3]),
    .out4(decoder_1_out0[4]), .out5(decoder_1_out0[5]), .out6(decoder_1_out0[6]), .out7(decoder_1_out0[7]),
    .sel(\Командный_регистр_q [2:0]));  // open: en
  and and_3 (and_9_out[4], decoder_1_out0[4], rom_1_data[7]);
  and and_4 (and_9_out[5], decoder_1_out0[5], rom_1_data[7]);
  assign \Шина  = rom_1_data[15] ? \Счетчик_команд_2_q  : 8'bz;  // Controlled_Buffer controlled_buffer_1
  ROM #(.addrWidth(7), .dataWidth(18)) rom_1 (
    .addr({\Командный_регистр_q [7:4], \Счетчик_команд_q }),
    .data({rom_1_data[17], rom_1_data_2[7], rom_1_data[15:0]}));  // open: sel
  and and_5 (and_9_out[2], decoder_1_out0[2], rom_1_data[7]);
  and and_6 (and_9_out[3], decoder_1_out0[3], rom_1_data[7]);
  assign and_7_out = decoder_1_out0 & {8{rom_1_data[8]}};  // AND_Gate and_7, 8 bits wide
  and and_8 (and_9_out[1], decoder_1_out0[1], rom_1_data[7]);
  and and_9 (and_9_out[0], decoder_1_out0[0], rom_1_data[7]);
  Clock \u_Тактовый_генератор  (.out(\Тактовый_генератор_out ));
  assign controlled_buffer_2_out = not_1_out ? \Тактовый_генератор_out  : 1'bz;  // Controlled_Buffer controlled_buffer_2
  assign \Шина  = rom_1_data[12] ? \Командный_регистр_q  : 8'bz;  // Controlled_Buffer controlled_buffer_3
  Pull_Resistor pull_resistor_1 (.node(controlled_buffer_2_out));
  Pull_Resistor pull_resistor_2 (.node(\Сброс ));
  Pull_Resistor pull_resistor_3 (.node(\Шина ));
  assign \Шина  = and_9_out[1] ? \Регистр_1_q  : 8'bz;  // Controlled_Buffer controlled_buffer_4
  Register \u_Адресный_регистр  (
    .D(\Шина ), .en(rom_1_data[11]), .Q(\Адресный_регистр_q ), .clk(controlled_buffer_2_out), .clr(\Сброс ));
  Register \u_Регистр_0  (
    .D(\Шина ), .en(and_7_out[0]), .Q(\Регистр_0_q ), .clk(controlled_buffer_2_out), .clr(\Сброс ));
  Adder adder_1 (.a(\Регистр_0_q ), .b(\Регистр_1_q ), .out(adder_1_out));  // open: cin, cout
  Register \u_Регистр_1  (
    .D(\Шина ), .en(and_7_out[1]), .Q(\Регистр_1_q ), .clk(controlled_buffer_2_out), .clr(\Сброс ));
  Register \u_Регистр_2  (
    .D(\Шина ), .en(and_7_out[2]), .Q(\Регистр_2_q ), .clk(controlled_buffer_2_out), .clr(\Сброс ));
  Register \u_Регистр_3  (
    .D(\Шина ), .en(and_7_out[3]), .Q(\Регистр_3_q ), .clk(controlled_buffer_2_out), .clr(\Сброс ));
  Register \u_Регистр_4  (
    .D(\Шина ), .en(and_7_out[4]), .Q(\Регистр_4_q ), .clk(controlled_buffer_2_out), .clr(\Сброс ));
  Register \u_Регистр_5  (
    .D(\Шина ), .en(and_7_out[5]), .Q(\Регистр_5_q ), .clk(controlled_buffer_2_out), .clr(\Сброс ));
  Register JR (.D(\Шина ), .en(rom_1_data[5]), .Q(JR_q), .clk(controlled_buffer_2_out), .clr(\Сброс ));
  assign \Шина  = or_1_out ? JR_q : 8'bz;  // Controlled_Buffer controlled_buffer_5
  assign \Шина  = and_10_out ? RTSK_q : 8'bz;  // Controlled_Buffer controlled_buffer_6
  and and_10 (and_10_out, ~or_1_out, rom_1_data[4]);  // AND_Gate
  assign \Шина  = rom_1_data[10] ? ram_1_data : 8'bz;  // Controlled_Buffer controlled_buffer_7
  assign \Шина  = and_9_out[0] ? \Регистр_0_q  : 8'bz;  // Controlled_Buffer controlled_buffer_8
  assign \Шина  = rom_1_data[6] ? adder_1_out : 8'bz;  // Controlled_Buffer controlled_buffer_9
  assign \Шина  = and_9_out[2] ? \Регистр_2_q  : 8'bz;  // Controlled_Buffer controlled_buffer_10
  assign \Шина  = and_9_out[3] ? \Регистр_3_q  : 8'bz;  // Controlled_Buffer controlled_buffer_11
  assign \Шина  = and_9_out[4] ? \Регистр_4_q  : 8'bz;  // Controlled_Buffer controlled_buffer_12
  assign \Шина  = and_9_out[5] ? \Регистр_5_q  : 8'bz;  // Controlled_Buffer controlled_buffer_13
  and and_11 (and_11_out, rom_1_data[3], or_4_out);
  or or_1 (or_1_out, and_11_out, and_12_out);
  and and_12 (and_12_out, or_3_out, rom_1_data[2]);
  Register RTSK (.D(\Шина ), .en(rom_1_data[1]), .Q(RTSK_q), .clk(controlled_buffer_2_out), .clr(\Сброс ));
  or or_2 (or_2_out, rom_1_data[10], rom_1_data[9]);
  assign xor_1_out = \Регистр_1_q  ^ {8{rom_1_data_2[7]}};  // XOR_Gate xor_1, 8 bits wide
  \с81  \u_с81_1  (.A(\Регистр_2_q ), .B(\Регистр_3_q ), .A_B_2(\с81_1_a_b_2 ), .A_B_3(\с81_1_a_b_3 ));  // open: A_B
  \с8  \u_с8_1  (.A(\Регистр_4_q ), .B(\Регистр_5_q ), .A_B_2(\с8_1_a_b_2 ), .A_B_3(\с8_1_a_b_3 ));  // open: A_B
  or or_3 (or_3_out, \с8_1_a_b_3 , \с8_1_a_b_2 );
  RAM #(.bus("separate")) ram_1 (
    .addr(\Адресный_регистр_q ), .din(\Шина ), .data(ram_1_data), .str(rom_1_data[9]), .sel(or_2_out),
    .clk(controlled_buffer_2_out), .ld(rom_1_data[10]), .clr(\Очистка_памяти ));
  assign \Шина  = rom_1_data_2[7] ? adder_2_out : 8'bz;  // Controlled_Buffer controlled_buffer_14
  Adder adder_2 (.a(\Регистр_0_q ), .b(adder_3_out), .out(adder_2_out));  // open: cin, cout
  Pull_Resistor pull_resistor_4 (.node(pull_resistor_6_node[7]));
  Adder adder_3 (.a(xor_1_out), .b({pull_resistor_6_node, rom_1_data_2[7]}), .out(adder_3_out));  // open: cin, cout
  and and_13 (and_13_out, \с81_1_a_b_2 , \с8_1_a_b_3 );
  Pull_Resistor pull_resistor_5 (.node(pull_resistor_6_node[5]));
  Pull_Resistor pull_resistor_6 (.node(pull_resistor_6_node[1]));
  Pull_Resistor pull_resistor_7 (.node(pull_resistor_6_node[3]));
  Pull_Resistor pull_resistor_8 (.node(pull_resistor_6_node[2]));
  Pull_Resistor pull_resistor_9 (.node(pull_resistor_6_node[4]));
  Pull_Resistor pull_resistor_10 (.node(pull_resistor_6_node[6]));
  or or_4 (or_4_out, \с81_1_a_b_3 , and_13_out);
  Hex_Digit_Display hex_digit_display_1 (.value(bit_extender_1_out));  // open: dp
  Bit_Extender #(.in_width(16), .out_width(4)) bit_extender_1 (.in(divider_1_out), .out(bit_extender_1_out));
  Hex_Digit_Display hex_digit_display_2 (.value(bit_extender_2_out));  // open: dp
  Hex_Digit_Display hex_digit_display_3 (.value(bit_extender_3_out));  // open: dp
  Divider #(.width(16)) divider_1 (
    .a(register_1_q), .b(16'h2710), .out(divider_1_out), .rem(divider_1_rem));  // open: upper
  Divider #(.width(16)) divider_2 (
    .a(divider_1_rem), .b(16'h3e8), .out(divider_2_out), .rem(divider_2_rem));  // open: upper
  Divider #(.width(16)) divider_3 (
    .a(divider_2_rem), .b(16'h64), .out(divider_3_out), .rem(divider_3_rem));  // open: upper
  Hex_Digit_Display hex_digit_display_4 (.value(bit_extender_5_out));  // open: dp
  Hex_Digit_Display hex_digit_display_5 (.value(bit_extender_4_out));  // open: dp
  Bit_Extender #(.in_width(16), .out_width(4)) bit_extender_2 (.in(divider_2_out), .out(bit_extender_2_out));
  Bit_Extender #(.in_width(16), .out_width(4)) bit_extender_3 (.in(divider_3_out), .out(bit_extender_3_out));
  Bit_Extender #(.in_width(16), .out_width(4)) bit_extender_4 (.in(divider_4_out), .out(bit_extender_4_out));
  Divider #(.width(16)) divider_4 (
    .a(divider_3_rem), .b(16'ha), .out(divider_4_out), .rem(divider_4_rem));  // open: upper
  Bit_Extender #(.in_width(16), .out_width(4)) bit_extender_5 (.in(divider_4_rem), .out(bit_extender_5_out));
  Register #(.width(16)) register_1 (
    .D({\Регистр_2_q , \Регистр_4_q }), .en(rom_1_data[17]), .Q(register_1_q), .clk(controlled_buffer_2_out),
    .clr(\Сброс ));

  // Notes on the sheet:
  //   contents of rom_1 (hex, n*v repeats v):
  //   4*0 8800 6400 0 0 8800 4500 880 500 8800 6400 0 0 8800 4500 0 0 8800 6400 0 0 8800 4402 810 280 8800
  //   6400 0 0 10100 0 0 0 8800 6400 0 0 140 0 0 0 8800 6400 0 0 8800 402 811 2400 8800 6400 0 0 8802 4420
  //   819 4000 8800 6400 0 0 8802 4420 815 4000 8800 6400 0 0 840 500 810 0 8800 6400 0 0 840 280 810 0
  //   8800 6400 0 0 20000 0 0 0 8800 6400 6*0 8800 6400
endmodule

module compare (
  input  less_than,
  input  equal,
  input  more_than,
  input  less_than__2,
  input  equal__2,
  input  more_than__2,
  output LESS,
  output EQUAL_2,
  output MORE
);

  wire and_1_out, and_2_out, and_3_out, and_4_out, and_5_out, and_6_out, and_7_out, and_9_out, not_1_out,
       not_2_out, not_3_out, not_4_out, not_5_out, not_6_out, not_7_out, not_8_out, not_9_out, not_10_out,
       not_11_out, not_12_out, not_13_out, not_14_out, not_15_out, not_16_out, not_17_out, not_18_out,
       not_19_out, not_20_out, not_21_out, not_22_out, not_23_out, not_24_out, not_25_out, not_26_out,
       not_27_out, not_28_out, not_29_out, not_30_out, not_31_out, not_32_out, not_33_out, not_34_out,
       not_35_out, not_36_out;

  not not_1 (not_1_out, less_than);
  not not_2 (not_2_out, equal);
  not not_3 (not_3_out, equal__2);
  not not_4 (not_4_out, more_than__2);
  not not_5 (not_5_out, less_than);
  not not_6 (not_6_out, equal);
  not not_7 (not_7_out, less_than__2);
  not not_8 (not_8_out, equal__2);
  and and_1 (and_1_out, not_1_out, not_2_out, more_than, less_than__2, not_3_out, not_4_out);
  not not_9 (not_9_out, less_than);
  not not_10 (not_10_out, more_than);
  not not_11 (not_11_out, equal__2);
  not not_12 (not_12_out, more_than__2);
  and and_2 (and_2_out, not_5_out, not_6_out, more_than, not_7_out, not_8_out, more_than__2);
  not not_13 (not_13_out, less_than);
  not not_14 (not_14_out, equal);
  not not_15 (not_15_out, less_than__2);
  not not_16 (not_16_out, more_than__2);
  and and_3 (and_3_out, not_9_out, equal, not_10_out, less_than__2, not_11_out, not_12_out);
  not not_17 (not_17_out, equal);
  not not_18 (not_18_out, more_than);
  not not_19 (not_19_out, less_than__2);
  not not_20 (not_20_out, more_than__2);
  and and_4 (and_4_out, not_13_out, not_14_out, more_than, not_15_out, equal__2, not_16_out);
  not not_21 (not_21_out, less_than);
  not not_22 (not_22_out, more_than);
  not not_23 (not_23_out, less_than__2);
  not not_24 (not_24_out, equal__2);
  and and_5 (and_5_out, less_than, not_17_out, not_18_out, not_19_out, equal__2, not_20_out);
  not not_25 (not_25_out, equal);
  not not_26 (not_26_out, more_than);
  not not_27 (not_27_out, equal__2);
  not not_28 (not_28_out, more_than__2);
  not not_29 (not_29_out, less_than);
  not not_30 (not_30_out, more_than);
  not not_31 (not_31_out, less_than__2);
  not not_32 (not_32_out, more_than__2);
  and and_6 (and_6_out, not_21_out, equal, not_22_out, not_23_out, not_24_out, more_than__2);
  not not_33 (not_33_out, equal);
  not not_34 (not_34_out, more_than);
  not not_35 (not_35_out, less_than__2);
  not not_36 (not_36_out, equal__2);
  and and_7 (and_7_out, less_than, not_25_out, not_26_out, less_than__2, not_27_out, not_28_out);
  and and_8 (EQUAL_2, not_29_out, equal, not_30_out, not_31_out, equal__2, not_32_out);
  and and_9 (and_9_out, less_than, not_33_out, not_34_out, not_35_out, not_36_out, more_than__2);
  or or_1 (LESS, and_1_out, and_3_out, and_5_out, and_7_out);
  or or_2 (MORE, and_2_out, and_4_out, and_6_out, and_9_out);
endmodule

module \с4  (
  input  [3:0] A,
  input  [3:0] B,
  input  a_b,
  input  a_b_2,
  input  a_b_3,
  output A_B_4,
  output A_B_5,
  output A_B_6
);

  wire and_1_out, and_2_out, and_3_out, and_4_out, and_5_out, nor_1_out, not_1_out, not_2_out, not_3_out,
       not_4_out, or_1_out, xnor_1_out, xnor_2_out, xnor_3_out, xnor_4_out;

  xnor xnor_1 (xnor_1_out, A[0], B[0]);
  xnor xnor_2 (xnor_2_out, A[1], B[1]);
  xnor xnor_3 (xnor_3_out, A[2], B[2]);
  xnor xnor_4 (xnor_4_out, A[3], B[3]);
  not not_1 (not_1_out, B[0]);
  not not_2 (not_2_out, B[1]);
  not not_3 (not_3_out, B[2]);
  not not_4 (not_4_out, B[3]);
  and and_1 (and_1_out, xnor_4_out, xnor_3_out, xnor_2_out, not_1_out, A[0]);
  and and_2 (and_2_out, xnor_4_out, xnor_3_out, not_2_out, A[1]);
  and and_3 (and_3_out, xnor_4_out, not_3_out, A[2]);
  and and_4 (and_4_out, not_4_out, A[3]);
  and and_5 (and_5_out, xnor_1_out, xnor_2_out, xnor_3_out, xnor_4_out);
  or or_1 (or_1_out, and_1_out, and_2_out, and_3_out, and_4_out);
  nor nor_1 (nor_1_out, and_5_out, or_1_out);
  compare compare_1 (
    .less_than(a_b), .equal(a_b_2), .more_than(a_b_3), .less_than__2(nor_1_out), .equal__2(and_5_out),
    .more_than__2(or_1_out), .LESS(A_B_4), .EQUAL_2(A_B_5), .MORE(A_B_6));
endmodule

module \с8  (
  input  [7:0] A,
  input  [7:0] B,
  output A_B,
  output A_B_2,
  output A_B_3
);

  wire a_t, pull_resistor_2_node, pull_resistor_3_node, pull_resistor_4_node, \с4_1_a_b_4 , \с4_1_a_b_5 ,
       \с4_1_a_b_6 , \с4_2_a_b_4 , \с4_2_a_b_5 , \с4_2_a_b_6 ;

  assign A_B = a_t ? A[7] : 1'bz;  // Controlled_Buffer controlled_buffer_1
  Pull_Resistor pull_resistor_1 (.node(A_B));
  xor xor_1 (a_t, B[7], A[7]);
  Pull_Resistor #(.pull(1)) pull_resistor_2 (.node(pull_resistor_2_node));
  Pull_Resistor pull_resistor_3 (.node(pull_resistor_3_node));
  Pull_Resistor pull_resistor_4 (.node(pull_resistor_4_node));
  not not_1 (pull_resistor_4_node, a_t);
  \с4  \u_с4_1  (
    .A(A[3:0]), .B(B[3:0]), .a_b(pull_resistor_3_node), .a_b_2(pull_resistor_2_node),
    .a_b_3(pull_resistor_3_node), .A_B_4(\с4_1_a_b_4 ), .A_B_5(\с4_1_a_b_5 ), .A_B_6(\с4_1_a_b_6 ));
  \с4  \u_с4_2  (
    .A(A[7:4]), .B(B[7:4]), .a_b(\с4_1_a_b_4 ), .a_b_2(\с4_1_a_b_5 ), .a_b_3(\с4_1_a_b_6 ),
    .A_B_4(\с4_2_a_b_4 ), .A_B_5(\с4_2_a_b_5 ), .A_B_6(\с4_2_a_b_6 ));
  assign A_B_2 = pull_resistor_4_node ? \с4_2_a_b_5  : 1'bz;  // Controlled_Buffer controlled_buffer_2
  assign A_B_3 = pull_resistor_4_node ? \с4_2_a_b_6  : 1'bz;  // Controlled_Buffer controlled_buffer_3
  assign A_B_3 = a_t ? ~A_B : 1'bz;  // Controlled_Inverter controlled_inverter_1
  assign A_B = pull_resistor_4_node ? \с4_2_a_b_4  : 1'bz;  // Controlled_Buffer controlled_buffer_4
  Pull_Resistor pull_resistor_5 (.node(A_B_2));
endmodule

module \с81  (
  input  [7:0] A,
  input  [7:0] B,
  output A_B,
  output A_B_2,
  output A_B_3
);

  wire pull_resistor_1_node, pull_resistor_2_node, \с4_1_a_b_4 , \с4_1_a_b_5 , \с4_1_a_b_6 ;

  Pull_Resistor pull_resistor_1 (.node(pull_resistor_1_node));
  Pull_Resistor #(.pull(1)) pull_resistor_2 (.node(pull_resistor_2_node));
  \с4  \u_с4_1  (
    .A(A[3:0]), .B(B[3:0]), .a_b(pull_resistor_1_node), .a_b_2(pull_resistor_2_node),
    .a_b_3(pull_resistor_1_node), .A_B_4(\с4_1_a_b_4 ), .A_B_5(\с4_1_a_b_5 ), .A_B_6(\с4_1_a_b_6 ));
  \с4  \u_с4_2  (
    .A(A[7:4]), .B(B[7:4]), .a_b(\с4_1_a_b_4 ), .a_b_2(\с4_1_a_b_5 ), .a_b_3(\с4_1_a_b_6 ), .A_B_4(A_B),
    .A_B_5(A_B_2), .A_B_6(A_B_3));
endmodule
